// Logisim project LVDC.circ as structural Verilog: 7 circuits, main circuit main
module main (
  input  master_rst,
  input  IRUPT,
  output [25:0] IOBUS,
  output [7:0] IOADDR,
  output IOR,
  output IOW
);

  wire and_1_out, and_2_out, and_3_out, and_4_out, and_5_out, and_6_out, and_7_out, and_8_out, and_9_out,
       and_10_out, and_11_out, and_12_out, and_13_out, and_14_out, and_15_out, and_16_out, and_17_out,
       and_18_out, and_19_out, comparator_1_eq, comparator_2_eq, comparator_3_eq, d_ff_1_qn, d_ff_2_q,
       d_ff_3_q, d_ff_4_q, d_ff_4_qn, IRUPT_MASK_q, IRUPT_MASK_qn, memory_1_hop_instead_of_a,
       memory_1_pq_addr, muldiv_1_is_active, multiplexer_2_out, multiplexer_3_out, n74163_1_pin1,
       n74163_1_pin2, n74163_1_pin3, n74163_1_pin7, n74163_1_pin10, nand_1_out, not_1_out, not_2_out,
       not_3_out, not_4_out, not_6_out, not_7_out, not_8_out, not_9_out, not_10_out, not_11_out, not_12_out,
       not_13_out, not_14_out, not_16_out, not_17_out, not_18_out, not_19_out, or_1_out, or_2_out, or_3_out,
       or_4_out, or_5_out, or_6_out, or_9_out, or_10_out, or_11_out, registers_1_csyllable;
  wire [2:0] controlled_buffer_1_out_3, EXM_SECTOR_q, multiplexer_1_out, registers_1_data_module,
       registers_1_instr_module;
  wire [3:0] and_20_out, controlled_buffer_1_out, controlled_buffer_1_out_2, registers_1_data_sector,
       registers_1_instr_sector;
  wire [3:3] not_15_out;
  wire [7:0] registers_1_instr_address;
  wire [8:7] controlled_buffer_1_out_4, or_8_out;
  wire [10:0] n74163_1_pin14;
  wire [12:0] controlled_buffer_3_out;
  wire [15:0] instructiondecode_1_dout;
  wire [25:0] registers_1_accum;

  not not_1 (not_1_out, muldiv_1_is_active);
  and and_1 (and_1_out, IRUPT, not_1_out);
  D_Flip_Flop d_ff_1 (.D(and_1_out), .clk(n74163_1_pin2), .Qn(d_ff_1_qn));  // open: Q, preset, reset
  and and_2 (and_2_out, nand_1_out, or_1_out);
  or or_1 (or_1_out, IRUPT_MASK_q, and_5_out);
  not not_2 (not_2_out, and_5_out);
  and and_3 (and_3_out, and_1_out, IRUPT_MASK_qn, d_ff_1_qn);
  D_Flip_Flop IRUPT_MASK (
    .D(and_2_out), .clk(n74163_1_pin2), .Q(IRUPT_MASK_q), .Qn(IRUPT_MASK_qn), .reset(master_rst));  // open: preset
  or or_2 (or_2_out, and_3_out, d_ff_2_q);
  D_Flip_Flop d_ff_2 (.D(and_4_out), .clk(n74163_1_pin2), .Q(d_ff_2_q));  // open: Qn, preset, reset
  and and_4 (and_4_out, not_2_out, or_2_out);
  and and_5 (and_5_out, d_ff_2_q, and_12_out);
  D_Flip_Flop d_ff_3 (.D(and_5_out), .clk(n74163_1_pin2), .Q(d_ff_3_q));  // open: Qn, preset, reset
  and and_6 (and_6_out, instructiondecode_1_dout[5], d_ff_4_q);
  or or_3 (or_3_out, d_ff_3_q, and_5_out);
  not not_3 (not_3_out, instructiondecode_1_dout[14]);
  not not_4 (not_4_out, instructiondecode_1_dout[15]);
  _74163 u_74163_1 (
    .pin1(n74163_1_pin1), .pin2(n74163_1_pin2), .pin3(n74163_1_pin3), .pin4(n74163_1_pin3),
    .pin5(n74163_1_pin3), .pin6(n74163_1_pin3), .pin7(n74163_1_pin7), .pin14(n74163_1_pin14[0]),
    .pin13(n74163_1_pin14[1]), .pin12(n74163_1_pin14[2]), .pin10(n74163_1_pin10), .pin9(n74163_1_pin10));  // open: pin15, pin11
  not not_5 (n74163_1_pin1, or_4_out);
  or or_4 (or_4_out, master_rst, instructiondecode_1_dout[5]);
  or or_5 (or_5_out, instructiondecode_1_dout[10], and_6_out);
  and and_7 (and_7_out, instructiondecode_1_dout[14], instructiondecode_1_dout[15]);
  and and_8 (and_8_out, not_3_out, instructiondecode_1_dout[15]);
  and and_9 (and_9_out, instructiondecode_1_dout[14], not_4_out);
  Multiplexer #(.width(3)) multiplexer_1 (
    .in0(EXM_SECTOR_q), .in1(controlled_buffer_1_out_3), .out(multiplexer_1_out),
    .sel(instructiondecode_1_dout[12]));
  and and_10 (and_10_out, n74163_1_pin14[2], and_7_out);
  and and_11 (and_11_out, and_7_out, not_6_out);
  not not_6 (not_6_out, n74163_1_pin14[2]);
  and and_12 (and_12_out, instructiondecode_1_dout[10], d_ff_4_qn);
  Multiplexer multiplexer_2 (
    .in0(d_ff_4_q), .in1(instructiondecode_1_dout[12]), .out(multiplexer_2_out), .sel(or_5_out));
  Register #(.width(3)) EXM_SECTOR (
    .D(multiplexer_1_out), .en(1'b1), .clk(n74163_1_pin2), .Q(EXM_SECTOR_q), .clr(master_rst));
  Clock clock_1 (.out(n74163_1_pin2));
  not not_7 (not_7_out, instructiondecode_1_dout[12]);
  and and_13 (and_13_out, not_7_out, instructiondecode_1_dout[5]);
  D_Flip_Flop d_ff_4 (
    .D(multiplexer_2_out), .clk(n74163_1_pin2), .Q(d_ff_4_q), .Qn(d_ff_4_qn), .reset(master_rst));  // open: preset
  not not_8 (not_8_out, and_11_out);
  InstructionDecode instructiondecode_1 (
    .DIN({n74163_1_pin14[10:9], IOADDR[7], n74163_1_pin14[7:0]}), .DOUT(instructiondecode_1_dout));
  not not_9 (not_9_out, not_8_out);
  not not_10 (not_10_out, comparator_1_eq);
  and and_14 (and_14_out, not_10_out, and_9_out);
  and and_15 (and_15_out, and_9_out, comparator_1_eq);
  Hex_Digit_Display hex_digit_display_1 (.value({2'b00, IOBUS[25:24]}));  // open: dp
  Pull_Resistor pull_resistor_1 (.node(IOBUS));
  not not_11 (not_11_out, and_19_out);
  Hex_Digit_Display hex_digit_display_2 (.value(IOBUS[23:20]));  // open: dp
  Hex_Digit_Display hex_digit_display_3 (.value(IOBUS[19:16]));  // open: dp
  and and_16 (and_16_out, and_19_out, instructiondecode_1_dout[4]);
  and and_17 (and_17_out, not_11_out, instructiondecode_1_dout[4]);
  Hex_Digit_Display hex_digit_display_4 (.value(IOBUS[15:12]));  // open: dp
  Hex_Digit_Display hex_digit_display_5 (.value(IOBUS[11:8]));  // open: dp
  ALU alu_1 (
    .ACCUM(registers_1_accum), .ALU_BUSI(IOBUS), .IS_RSU(instructiondecode_1_dout[0]), .CLK(n74163_1_pin2),
    .RST(master_rst), .ALU_R(instructiondecode_1_dout[1]),
    .ALU_SSEL({IOADDR[0], IOADDR[1], IOADDR[4], IOADDR[5]}), .ALU_ISS(instructiondecode_1_dout[2]),
    .op0(n74163_1_pin14[3]), .op1(n74163_1_pin14[4]), .op2(n74163_1_pin14[5]), .op3(n74163_1_pin14[6]),
    .TO_BUS(IOBUS));
  Registers registers_1 (
    .BUSI(IOBUS), .ACCW(instructiondecode_1_dout[3]), .CLK(n74163_1_pin2), .RSTI(master_rst),
    .R_A(and_17_out), .CDS(instructiondecode_1_dout[6]), .TRA(instructiondecode_1_dout[8]),
    .INCPC(and_13_out), .R_H(and_16_out), .HOPW(instructiondecode_1_dout[7]),
    .H_CYC_1(instructiondecode_1_dout[5]), .INSTR_ADDR_I({IOADDR, n74163_1_pin14[7]}),
    .CSYLLABLE(registers_1_csyllable), .INSTR_SECTOR(registers_1_instr_sector), .ACCUM(registers_1_accum),
    .INSTR_MODULE(registers_1_instr_module), .BUSO(IOBUS), .INSTR_ADDRESS(registers_1_instr_address),
    .DATA_SECTOR(registers_1_data_sector), .DATA_MODULE(registers_1_data_module),
    .ACCUM_ZERO(n74163_1_pin14[9]), .ACCUM_NEGATIVE(n74163_1_pin14[10]));
  Memory memory_1 (
    .INSTR_MODULE_I(registers_1_instr_module), .INSTR_SECTOR_I(registers_1_instr_sector),
    .PCI(registers_1_instr_address), .FETCH_CYC(instructiondecode_1_dout[10]),
    .MEM_WR(instructiondecode_1_dout[9]), .DATA_MODULE_I(registers_1_data_module), .M_BUSI(IOBUS),
    .MEM_RD(instructiondecode_1_dout[11]), .irupt(d_ff_3_q), .DATA_SECTOR_I(registers_1_data_sector),
    .EXM_EXEC_I(d_ff_4_q), .EXM_SECTOR(EXM_SECTOR_q), .RESIDUAL_I(n74163_1_pin14[7]),
    .IS_EXM_I(instructiondecode_1_dout[12]), .OPADDR_I(IOADDR), .CLKIR(n74163_1_pin2), .M_BUSO(IOBUS),
    .PQ_ADDR(memory_1_pq_addr), .HOP_INSTEAD_OF_A(memory_1_hop_instead_of_a));
  Hex_Digit_Display hex_digit_display_6 (.value(IOBUS[7:4]));  // open: dp
  Hex_Digit_Display hex_digit_display_7 (.value(IOBUS[3:0]));  // open: dp
  or or_6 (or_6_out, and_10_out, memory_1_pq_addr);
  LED led_1 (.in(or_6_out));
  Hex_Digit_Display hex_digit_display_8 (.value({2'b00, registers_1_accum[25:24]}));  // open: dp
  Hex_Digit_Display hex_digit_display_9 (.value(registers_1_accum[23:20]));  // open: dp
  muldiv muldiv_1 (
    .OUTPUT_PQ(or_6_out), .RST(not_9_out), .CLK(n74163_1_pin2), .MD_BUSI(IOBUS), .LDX(and_14_out),
    .LDY(and_8_out), .IS_DIV(comparator_1_eq), .LDZ(and_15_out), .START(and_8_out), .MD_BUSO(IOBUS),
    .IS_ACTIVE(muldiv_1_is_active));
  Hex_Digit_Display hex_digit_display_10 (.value(registers_1_accum[19:16]));  // open: dp
  Hex_Digit_Display hex_digit_display_11 (.value(registers_1_accum[15:12]));  // open: dp
  LED led_2 (.in(muldiv_1_is_active));
  and and_18 (and_18_out, comparator_2_eq, muldiv_1_is_active);
  Hex_Digit_Display hex_digit_display_12 (.value(registers_1_accum[11:8]));  // open: dp
  Hex_Digit_Display hex_digit_display_13 (.value(registers_1_accum[7:4]));  // open: dp
  Comparator #(.mode("unsigned"), .width(4)) comparator_1 (
    .a(4'b0011), .b(n74163_1_pin14[6:3]), .eq(comparator_1_eq));  // open: gt, lt
  Comparator #(.mode("unsigned"), .width(4)) comparator_2 (
    .a(4'b0101), .b(n74163_1_pin14[6:3]), .eq(comparator_2_eq));  // open: gt, lt
  D_Flip_Flop d_ff_5 (.D(and_18_out), .clk(n74163_1_pin2), .Qn(n74163_1_pin7), .reset(master_rst));  // open: Q, preset
  Hex_Digit_Display hex_digit_display_14 (.value(registers_1_accum[3:0]));  // open: dp
  assign {controlled_buffer_1_out_2, controlled_buffer_1_out_4, controlled_buffer_1_out_3, controlled_buffer_1_out} = not_12_out ? IOBUS[12:0] : 13'bz;  // Controlled_Buffer controlled_buffer_1
  not not_12 (not_12_out, multiplexer_3_out);
  assign {controlled_buffer_1_out_2, controlled_buffer_1_out_4, controlled_buffer_1_out_3, controlled_buffer_1_out} = multiplexer_3_out ? IOBUS[25:13] : 13'bz;  // Controlled_Buffer controlled_buffer_2
  Multiplexer multiplexer_3 (
    .in0(registers_1_csyllable), .in1(IOADDR[4]), .out(multiplexer_3_out), .sel(instructiondecode_1_dout[12]));
  Register #(.trigger("falling"), .width(13)) INSIN (
    .D({controlled_buffer_3_out[12:4], and_20_out}), .en(1'b1), .clk(instructiondecode_1_dout[10]),
    .Q({IOADDR, n74163_1_pin14[7:3]}), .clr(master_rst));
  Hex_Digit_Display hex_digit_display_15 (.value(n74163_1_pin14[6:3]));  // open: dp
  not not_13 (not_13_out, n74163_1_pin14[6]);
  or or_7 (or_8_out[8], controlled_buffer_1_out_4[8], IOADDR[3]);
  or or_8 (or_8_out[7], IOADDR[2], controlled_buffer_1_out_4[7]);
  not not_14 (not_14_out, n74163_1_pin14[5]);
  not not_15 (not_15_out[3], or_3_out);
  not not_16 (not_16_out, n74163_1_pin14[3]);
  or or_9 (or_9_out, not_16_out, n74163_1_pin14[4]);
  or or_10 (or_10_out, not_14_out, not_13_out);
  assign controlled_buffer_3_out = instructiondecode_1_dout[12] ? {controlled_buffer_1_out_2, or_8_out, IOADDR[1:0], 1'b0, controlled_buffer_1_out} : 13'bz;  // Controlled_Buffer controlled_buffer_3
  assign controlled_buffer_3_out = not_17_out ? {controlled_buffer_1_out_2, controlled_buffer_1_out_4, controlled_buffer_1_out_3, controlled_buffer_1_out} : 13'bz;  // Controlled_Buffer controlled_buffer_4
  not not_17 (not_17_out, instructiondecode_1_dout[12]);
  or or_11 (or_11_out, or_9_out, or_10_out);
  not not_18 (not_18_out, or_11_out);
  and and_19 (and_19_out, not_18_out, memory_1_hop_instead_of_a);
  assign and_20_out = controlled_buffer_3_out[3:0] & {4{not_15_out[3]}};  // AND_Gate and_20, 4 bits wide
  Comparator comparator_3 (.a(IOADDR), .b(8'h1a), .eq(comparator_3_eq));  // open: gt, lt
  not not_19 (not_19_out, n74163_1_pin14[7]);
  and and_21 (IOR, n74163_1_pin14[7], instructiondecode_1_dout[13]);
  and and_22 (IOW, instructiondecode_1_dout[13], not_19_out);
  nand nand_1 (nand_1_out, n74163_1_pin14[7], comparator_3_eq);
  // also tied to GND on the sheet: n74163_1_pin3
  // also tied to VCC on the sheet: n74163_1_pin10

  // Notes on the sheet:
  //   BUS
  //   ACCUMULATOR
  //   Opcode
  //   EXM Modifier
endmodule

module ALU (
  input  [25:0] ACCUM,
  input  [25:0] ALU_BUSI,
  input  IS_RSU,
  input  CLK,
  input  RST,
  input  ALU_R,
  input  [3:0] ALU_SSEL,
  input  ALU_ISS,
  input  op0,
  input  op1,
  input  op2,
  input  op3,
  output [25:0] TO_BUS
);

  wire and_1_out, and_2_out, and_3_out, and_4_out, and_5_out, and_6_out, ls74181_1_cnp4, ls74181_2_cnp4,
       ls74181_3_cnp4, ls74181_4_cnp4, ls74181_5_cnp4, ls74181_6_cnp4, not_1_out, not_2_out, not_3_out,
       not_4_out, not_5_out, not_6_out, or_1_out, or_2_out, or_3_out, or_4_out;
  wire [25:0] controlled_buffer_1_out, controlled_buffer_3_out, controlled_buffer_5_out,
       controlled_buffer_7_out, ls74181_1_f0b, register_1_q;

  not not_1 (not_1_out, op0);
  not not_2 (not_2_out, op1);
  not not_3 (not_3_out, op2);
  not not_4 (not_4_out, op3);
  and and_1 (and_1_out, not_4_out, op0);
  and and_2 (and_2_out, not_4_out, op2);
  and and_3 (and_3_out, op2, not_1_out);
  not not_5 (not_5_out, IS_RSU);
  or or_1 (or_1_out, not_1_out, op3);
  or or_2 (or_2_out, not_2_out, not_3_out);
  assign controlled_buffer_1_out = not_5_out ? ACCUM : 26'bz;  // Controlled_Buffer controlled_buffer_1
  assign controlled_buffer_1_out = IS_RSU ? ALU_BUSI : 26'bz;  // Controlled_Buffer controlled_buffer_2
  assign controlled_buffer_3_out = IS_RSU ? ACCUM : 26'bz;  // Controlled_Buffer controlled_buffer_3
  assign controlled_buffer_3_out = not_5_out ? ALU_BUSI : 26'bz;  // Controlled_Buffer controlled_buffer_4
  and and_4 (and_4_out, op1, op2);
  and and_5 (and_5_out, op3, op1);
  or or_3 (or_3_out, and_5_out, and_3_out);
  and and_6 (and_6_out, not_3_out, not_2_out);
  or or_4 (or_4_out, or_3_out, and_6_out);
  LS74181 ls74181_1 (
    .Cn(and_1_out), .M(or_4_out), .A0b(controlled_buffer_1_out[0]), .B0b(controlled_buffer_3_out[0]),
    .A1b(controlled_buffer_1_out[1]), .B1b(controlled_buffer_3_out[1]), .A2b(controlled_buffer_1_out[2]),
    .B2b(controlled_buffer_3_out[2]), .A3b(controlled_buffer_1_out[3]), .B3b(controlled_buffer_3_out[3]),
    .S0(and_2_out), .S1(or_1_out), .S2(or_2_out), .S3(and_4_out), .F0b(ls74181_1_f0b[0]),
    .F1b(ls74181_1_f0b[1]), .F2b(ls74181_1_f0b[2]), .F3b(ls74181_1_f0b[3]), .Cnp4(ls74181_1_cnp4));  // open: AeqlB, Pb, Gp
  LS74181 ls74181_2 (
    .Cn(ls74181_1_cnp4), .M(or_4_out), .A0b(controlled_buffer_1_out[4]), .B0b(controlled_buffer_3_out[4]),
    .A1b(controlled_buffer_1_out[5]), .B1b(controlled_buffer_3_out[5]), .A2b(controlled_buffer_1_out[6]),
    .B2b(controlled_buffer_3_out[6]), .A3b(controlled_buffer_1_out[7]), .B3b(controlled_buffer_3_out[7]),
    .S0(and_2_out), .S1(or_1_out), .S2(or_2_out), .S3(and_4_out), .F0b(ls74181_1_f0b[4]),
    .F1b(ls74181_1_f0b[5]), .F2b(ls74181_1_f0b[6]), .F3b(ls74181_1_f0b[7]), .Cnp4(ls74181_2_cnp4));  // open: AeqlB, Pb, Gp
  LS74181 ls74181_3 (
    .Cn(ls74181_2_cnp4), .M(or_4_out), .A0b(controlled_buffer_1_out[8]), .B0b(controlled_buffer_3_out[8]),
    .A1b(controlled_buffer_1_out[9]), .B1b(controlled_buffer_3_out[9]), .A2b(controlled_buffer_1_out[10]),
    .B2b(controlled_buffer_3_out[10]), .A3b(controlled_buffer_1_out[11]), .B3b(controlled_buffer_3_out[11]),
    .S0(and_2_out), .S1(or_1_out), .S2(or_2_out), .S3(and_4_out), .F0b(ls74181_1_f0b[8]),
    .F1b(ls74181_1_f0b[9]), .F2b(ls74181_1_f0b[10]), .F3b(ls74181_1_f0b[11]), .Cnp4(ls74181_3_cnp4));  // open: AeqlB, Pb, Gp
  LS74181 ls74181_4 (
    .Cn(ls74181_3_cnp4), .M(or_4_out), .A0b(controlled_buffer_1_out[12]), .B0b(controlled_buffer_3_out[12]),
    .A1b(controlled_buffer_1_out[13]), .B1b(controlled_buffer_3_out[13]), .A2b(controlled_buffer_1_out[14]),
    .B2b(controlled_buffer_3_out[14]), .A3b(controlled_buffer_1_out[15]), .B3b(controlled_buffer_3_out[15]),
    .S0(and_2_out), .S1(or_1_out), .S2(or_2_out), .S3(and_4_out), .F0b(ls74181_1_f0b[12]),
    .F1b(ls74181_1_f0b[13]), .F2b(ls74181_1_f0b[14]), .F3b(ls74181_1_f0b[15]), .Cnp4(ls74181_4_cnp4));  // open: AeqlB, Pb, Gp
  LS74181 ls74181_5 (
    .Cn(ls74181_4_cnp4), .M(or_4_out), .A0b(controlled_buffer_1_out[16]), .B0b(controlled_buffer_3_out[16]),
    .A1b(controlled_buffer_1_out[17]), .B1b(controlled_buffer_3_out[17]), .A2b(controlled_buffer_1_out[18]),
    .B2b(controlled_buffer_3_out[18]), .A3b(controlled_buffer_1_out[19]), .B3b(controlled_buffer_3_out[19]),
    .S0(and_2_out), .S1(or_1_out), .S2(or_2_out), .S3(and_4_out), .F0b(ls74181_1_f0b[16]),
    .F1b(ls74181_1_f0b[17]), .F2b(ls74181_1_f0b[18]), .F3b(ls74181_1_f0b[19]), .Cnp4(ls74181_5_cnp4));  // open: AeqlB, Pb, Gp
  LS74181 ls74181_6 (
    .Cn(ls74181_5_cnp4), .M(or_4_out), .A0b(controlled_buffer_1_out[20]), .B0b(controlled_buffer_3_out[20]),
    .A1b(controlled_buffer_1_out[21]), .B1b(controlled_buffer_3_out[21]), .A2b(controlled_buffer_1_out[22]),
    .B2b(controlled_buffer_3_out[22]), .A3b(controlled_buffer_1_out[23]), .B3b(controlled_buffer_3_out[23]),
    .S0(and_2_out), .S1(or_1_out), .S2(or_2_out), .S3(and_4_out), .F0b(ls74181_1_f0b[20]),
    .F1b(ls74181_1_f0b[21]), .F2b(ls74181_1_f0b[22]), .F3b(ls74181_1_f0b[23]), .Cnp4(ls74181_6_cnp4));  // open: AeqlB, Pb, Gp
  LS74181 ls74181_7 (
    .Cn(ls74181_6_cnp4), .M(or_4_out), .A0b(controlled_buffer_1_out[24]), .B0b(controlled_buffer_3_out[24]),
    .A1b(controlled_buffer_1_out[25]), .B1b(controlled_buffer_3_out[25]), .A2b(1'b0), .B2b(1'b0), .A3b(1'b0),
    .B3b(1'b0), .S0(and_2_out), .S1(or_1_out), .S2(or_2_out), .S3(and_4_out), .F0b(ls74181_1_f0b[24]),
    .F1b(ls74181_1_f0b[25]));  // open: AeqlB, F2b, F3b, Pb, Cnp4, Gp
  assign controlled_buffer_5_out = ALU_ISS ? controlled_buffer_7_out : 26'bz;  // Controlled_Buffer controlled_buffer_5
  assign controlled_buffer_5_out = not_6_out ? ls74181_1_f0b : 26'bz;  // Controlled_Buffer controlled_buffer_6
  not not_6 (not_6_out, ALU_ISS);
  assign controlled_buffer_7_out = ALU_SSEL[0] ? {ACCUM[23:0], 2'b00} : 26'bz;  // Controlled_Buffer controlled_buffer_7
  assign controlled_buffer_7_out = ALU_SSEL[1] ? {ACCUM[24:0], 1'b0} : 26'bz;  // Controlled_Buffer controlled_buffer_8
  assign controlled_buffer_7_out = ALU_SSEL[2] ? {{3{ACCUM[25]}}, ACCUM[24:2]} : 26'bz;  // Controlled_Buffer controlled_buffer_9
  assign controlled_buffer_7_out = ALU_SSEL[3] ? {{2{ACCUM[25]}}, ACCUM[24:1]} : 26'bz;  // Controlled_Buffer controlled_buffer_10
  Register #(.width(26)) register_1 (.D(controlled_buffer_5_out), .en(1'b1), .clk(CLK), .Q(register_1_q), .clr(RST));
  Pull_Resistor pull_resistor_1 (.node(controlled_buffer_7_out));
  assign TO_BUS = ALU_R ? register_1_q : 26'bz;  // Controlled_Buffer controlled_buffer_11
endmodule

module LS74181 (
  input  Cn,
  input  M,
  input  A0b,
  input  B0b,
  input  A1b,
  input  B1b,
  input  A2b,
  input  B2b,
  input  A3b,
  input  B3b,
  input  S0,
  input  S1,
  input  S2,
  input  S3,
  output F0b,
  output F1b,
  output AeqlB,
  output F2b,
  output F3b,
  output Pb,
  output Cnp4,
  output Gp
);

  wire and_1_out, and_2_out, and_3_out, and_4_out, and_5_out, and_6_out, and_7_out, and_9_out, and_10_out,
       and_11_out, and_12_out, and_13_out, and_14_out, and_15_out, and_16_out, and_17_out, and_18_out,
       and_19_out, and_20_out, and_21_out, and_22_out, and_23_out, and_24_out, and_25_out, and_26_out,
       and_27_out, and_28_out, and_29_out, and_30_out, and_31_out, and_32_out, and_33_out, nand_1_out,
       nand_3_out, nor_1_out, nor_2_out, nor_3_out, nor_4_out, nor_5_out, nor_6_out, nor_7_out, nor_8_out,
       nor_9_out, nor_10_out, nor_11_out, not_1_out, not_2_out, not_3_out, not_4_out, not_5_out, not_6_out,
       not_7_out, not_8_out, not_9_out;

  not not_1 (not_1_out, M);
  nand nand_1 (nand_1_out, Cn, not_1_out);
  not not_2 (not_2_out, nor_1_out);
  and and_1 (and_1_out, not_2_out, nor_3_out);
  xor xor_1 (F0b, nand_1_out, and_1_out);
  and and_2 (and_2_out, not_1_out, nor_1_out);
  and and_3 (and_3_out, B0b, S0);
  nor nor_1 (nor_1_out, A0b, and_3_out, and_5_out);
  and and_4 (and_4_out, not_1_out, nor_3_out, Cn);
  nor nor_2 (nor_2_out, and_2_out, and_4_out);
  xor xor_2 (F1b, nor_2_out, and_7_out);
  and and_5 (and_5_out, S1, not_4_out);
  not not_3 (not_3_out, nor_5_out);
  not not_4 (not_4_out, B0b);
  and and_6 (and_6_out, not_4_out, S2, A0b);
  and and_7 (and_7_out, not_3_out, nor_6_out);
  and and_8 (AeqlB, F0b, F1b, F2b, F3b);
  and and_9 (and_9_out, A0b, B0b, S3);
  nor nor_3 (nor_3_out, and_6_out, and_9_out);
  and and_10 (and_10_out, not_1_out, nor_5_out);
  and and_11 (and_11_out, not_1_out, nor_1_out, nor_6_out);
  and and_12 (and_12_out, not_1_out, Cn, nor_3_out, nor_6_out);
  nor nor_4 (nor_4_out, and_10_out, and_11_out, and_12_out);
  xor xor_3 (F2b, nor_4_out, and_15_out);
  and and_13 (and_13_out, B1b, S0);
  nor nor_5 (nor_5_out, A1b, and_13_out, and_14_out);
  not not_5 (not_5_out, nor_8_out);
  not not_6 (not_6_out, B1b);
  and and_14 (and_14_out, S1, not_6_out);
  and and_15 (and_15_out, not_5_out, nor_9_out);
  and and_16 (and_16_out, not_6_out, S2, A1b);
  and and_17 (and_17_out, A1b, B1b, S3);
  nor nor_6 (nor_6_out, and_16_out, and_17_out);
  and and_18 (and_18_out, not_1_out, nor_8_out);
  and and_19 (and_19_out, not_1_out, nor_1_out, nor_6_out, nor_9_out);
  and and_20 (and_20_out, not_1_out, nor_5_out, nor_9_out);
  nor nor_7 (nor_7_out, and_18_out, and_20_out, and_19_out, and_22_out);
  xor xor_4 (F3b, nor_7_out, and_25_out);
  and and_21 (and_21_out, B2b, S0);
  nor nor_8 (nor_8_out, A2b, and_21_out, and_23_out);
  and and_22 (and_22_out, not_1_out, Cn, nor_3_out, nor_6_out, nor_9_out);
  not not_7 (not_7_out, B2b);
  and and_23 (and_23_out, S1, not_7_out);
  not not_8 (not_8_out, nor_10_out);
  and and_24 (and_24_out, not_7_out, S2, A2b);
  nor nor_9 (nor_9_out, and_24_out, and_26_out);
  and and_25 (and_25_out, not_8_out, nor_11_out);
  and and_26 (and_26_out, A2b, B2b, S3);
  nand nand_2 (Pb, nor_3_out, nor_6_out, nor_9_out, nor_11_out);
  nand nand_3 (nand_3_out, Cn, nor_3_out, nor_6_out, nor_9_out, nor_11_out);
  and and_27 (and_27_out, B3b, S0);
  and and_28 (and_28_out, S1, not_9_out);
  nor nor_10 (nor_10_out, A3b, and_27_out, and_28_out);
  or or_1 (Cnp4, ~nand_3_out, ~Gp);  // OR_Gate
  not not_9 (not_9_out, B3b);
  and and_29 (and_29_out, not_9_out, S2, A3b);
  and and_30 (and_30_out, nor_1_out, nor_6_out, nor_9_out, nor_11_out);
  and and_31 (and_31_out, A3b, B3b, S3);
  nor nor_11 (nor_11_out, and_29_out, and_31_out);
  and and_32 (and_32_out, nor_5_out, nor_9_out, nor_11_out);
  and and_33 (and_33_out, nor_8_out, nor_11_out);
  nor nor_12 (Gp, and_30_out, and_32_out, and_33_out, nor_10_out);
endmodule

module Registers (
  input  [25:0] BUSI,
  input  ACCW,
  input  CLK,
  input  RSTI,
  input  R_A,
  input  CDS,
  input  TRA,
  input  INCPC,
  input  R_H,
  input  HOPW,
  input  H_CYC_1,
  input  [8:0] INSTR_ADDR_I,
  output CSYLLABLE,
  output [3:0] INSTR_SECTOR,
  output [25:0] ACCUM,
  output [2:0] INSTR_MODULE,
  output [25:0] BUSO,
  output [7:0] INSTR_ADDRESS,
  output [3:0] DATA_SECTOR,
  output [2:0] DATA_MODULE,
  output ACCUM_ZERO,
  output ACCUM_NEGATIVE
);

  wire and_1_out, and_2_out, and_3_out, and_4_out, and_5_out, and_6_out, and_7_out, and_8_out, d_ff_1_qn,
       not_1_out, not_2_out, not_3_out, not_4_out, not_5_out, or_1_out, or_2_out, or_3_out, or_4_out,
       or_5_out, or_6_out, or_7_out, or_8_out, or_9_out, or_10_out, or_11_out, or_12_out, or_13_out,
       or_14_out, or_15_out, or_16_out, or_17_out, or_18_out, or_19_out, or_20_out, or_21_out, or_22_out,
       or_23_out, or_24_out, or_25_out, or_26_out;
  wire [14:7] not_7_out;
  wire [24:15] HOP_q;
  wire [25:0] controlled_buffer_1_out, controlled_buffer_2_out, LAST_HOP_q;

  and and_1 (and_1_out, INCPC, d_ff_1_qn);
  assign controlled_buffer_1_out = CDS ? {INSTR_MODULE[0], HOP_q[24], INSTR_ADDR_I[8:1], HOP_q[15], INSTR_ADDRESS, CSYLLABLE, INSTR_SECTOR, INSTR_MODULE[2:1]} : 26'bz;  // Controlled_Buffer controlled_buffer_1
  not not_1 (not_1_out, CDS);
  and and_2 (and_2_out, not_5_out, not_1_out, not_2_out, not_3_out);
  not not_2 (not_2_out, TRA);
  not not_3 (not_3_out, and_1_out);
  assign controlled_buffer_2_out = ACCW ? BUSI : 26'bz;  // Controlled_Buffer controlled_buffer_2
  assign controlled_buffer_2_out = not_4_out ? ACCUM : 26'bz;  // Controlled_Buffer controlled_buffer_3
  not not_4 (not_4_out, ACCW);
  assign controlled_buffer_1_out = and_1_out ? {INSTR_MODULE[0], HOP_q[24], DATA_SECTOR, DATA_MODULE, HOP_q[16:15], not_7_out, CSYLLABLE, INSTR_SECTOR, INSTR_MODULE[2:1]} : 26'bz;  // Controlled_Buffer controlled_buffer_4
  assign controlled_buffer_1_out = HOPW ? BUSI : 26'bz;  // Controlled_Buffer controlled_buffer_5
  assign controlled_buffer_1_out = and_2_out ? {INSTR_MODULE[0], HOP_q[24], DATA_SECTOR, DATA_MODULE, HOP_q[16:15], INSTR_ADDRESS, CSYLLABLE, INSTR_SECTOR, INSTR_MODULE[2:1]} : 26'bz;  // Controlled_Buffer controlled_buffer_6
  not not_5 (not_5_out, HOPW);
  D_Flip_Flop d_ff_1 (.D(or_1_out), .clk(CLK), .Qn(d_ff_1_qn));  // open: Q, preset, reset
  or or_1 (or_1_out, HOPW, TRA);
  or or_2 (or_2_out, ACCUM[0], ACCUM[1]);
  or or_3 (or_3_out, ACCUM[2], ACCUM[3]);
  or or_4 (or_4_out, ACCUM[4], ACCUM[5]);
  or or_5 (or_5_out, ACCUM[6], ACCUM[7]);
  or or_6 (or_6_out, ACCUM[8], ACCUM[9]);
  or or_7 (or_7_out, ACCUM[10], ACCUM[11]);
  or or_8 (or_8_out, ACCUM[12], ACCUM[13]);
  or or_9 (or_9_out, ACCUM[14], ACCUM[15]);
  or or_10 (or_10_out, ACCUM[16], ACCUM[17]);
  or or_11 (or_11_out, ACCUM[18], ACCUM[19]);
  or or_12 (or_12_out, ACCUM[20], ACCUM[21]);
  or or_13 (or_13_out, ACCUM[22], ACCUM[23]);
  or or_14 (or_14_out, ACCUM[24], ACCUM[25]);
  assign controlled_buffer_1_out = TRA ? {INSTR_MODULE[0], HOP_q[24], DATA_SECTOR, DATA_MODULE, HOP_q[16:15], INSTR_ADDR_I, INSTR_SECTOR, INSTR_MODULE[2:1]} : 26'bz;  // Controlled_Buffer controlled_buffer_7
  Register #(.width(26)) Accumulator (.D(controlled_buffer_2_out), .en(1'b1), .clk(CLK), .Q(ACCUM), .clr(RSTI));
  Register #(.width(26)) HOP (
    .D(controlled_buffer_1_out), .en(1'b1), .clk(CLK),
    .Q({INSTR_MODULE[0], HOP_q[24], DATA_SECTOR, DATA_MODULE, HOP_q[16:15], INSTR_ADDRESS, CSYLLABLE, INSTR_SECTOR, INSTR_MODULE[2:1]}),
    .clr(RSTI));
  Register #(.width(26)) LAST_HOP (
    .D({INSTR_MODULE[0], HOP_q[24], DATA_SECTOR, DATA_MODULE, HOP_q[16:15], not_7_out, CSYLLABLE, INSTR_SECTOR, INSTR_MODULE[2:1]}),
    .en(1'b1), .clk(H_CYC_1), .Q(LAST_HOP_q), .clr(RSTI));
  or or_15 (or_15_out, or_2_out, or_3_out);
  or or_16 (or_16_out, or_4_out, or_5_out);
  or or_17 (or_17_out, or_6_out, or_7_out);
  or or_18 (or_18_out, or_8_out, or_9_out);
  or or_19 (or_19_out, or_10_out, or_11_out);
  or or_20 (or_20_out, or_12_out, or_13_out);
  or or_21 (or_21_out, or_15_out, or_16_out);
  or or_22 (or_22_out, or_17_out, or_18_out);
  or or_23 (or_23_out, or_19_out, or_20_out);
  or or_24 (or_24_out, or_26_out, or_14_out);
  or or_25 (or_25_out, or_21_out, or_22_out);
  not not_6 (ACCUM_ZERO, or_24_out);
  assign BUSO = R_A ? ACCUM : 26'bz;  // Controlled_Buffer controlled_buffer_8
  assign BUSO = R_H ? LAST_HOP_q : 26'bz;  // Controlled_Buffer controlled_buffer_9
  or or_26 (or_26_out, or_25_out, or_23_out);
  not not_7 (not_7_out[7], INSTR_ADDRESS[0]);
  xor xor_1 (not_7_out[8], INSTR_ADDRESS[0], INSTR_ADDRESS[1]);
  and and_3 (and_3_out, INSTR_ADDRESS[0], INSTR_ADDRESS[1]);
  xor xor_2 (not_7_out[9], and_3_out, INSTR_ADDRESS[2]);
  and and_4 (and_4_out, and_3_out, INSTR_ADDRESS[2]);
  xor xor_3 (not_7_out[10], and_4_out, INSTR_ADDRESS[3]);
  and and_5 (and_5_out, and_4_out, INSTR_ADDRESS[3]);
  xor xor_4 (not_7_out[11], and_5_out, INSTR_ADDRESS[4]);
  and and_6 (and_6_out, and_5_out, INSTR_ADDRESS[4]);
  xor xor_5 (not_7_out[12], and_6_out, INSTR_ADDRESS[5]);
  and and_7 (and_7_out, and_6_out, INSTR_ADDRESS[5]);
  xor xor_6 (not_7_out[13], and_7_out, INSTR_ADDRESS[6]);
  and and_8 (and_8_out, and_7_out, INSTR_ADDRESS[6]);
  xor xor_7 (not_7_out[14], and_8_out, INSTR_ADDRESS[7]);

  assign ACCUM_NEGATIVE = ACCUM[25];

  // Notes on the sheet:
  //   reminder: that one 74-series that checks equality
endmodule

module Memory (
  input  [2:0] INSTR_MODULE_I,
  input  [3:0] INSTR_SECTOR_I,
  input  [7:0] PCI,
  input  FETCH_CYC,
  input  MEM_WR,
  input  [2:0] DATA_MODULE_I,
  input  [25:0] M_BUSI,
  input  MEM_RD,
  input  irupt,
  input  [3:0] DATA_SECTOR_I,
  input  EXM_EXEC_I,
  input  [2:0] EXM_SECTOR,
  input  RESIDUAL_I,
  input  IS_EXM_I,
  input  [7:0] OPADDR_I,
  input  CLKIR,
  output [25:0] M_BUSO,
  output PQ_ADDR,
  output HOP_INSTEAD_OF_A
);

  wire and_1_out, and_2_out, and_3_out, and_4_out, and_5_out, and_6_out, and_7_out, and_8_out, and_17_out,
       and_18_out, and_19_out, and_20_out, and_21_out, and_24_out, and_25_out, and_26_out,
       controlled_buffer_1_out, controlled_buffer_2_out, controlled_buffer_3_out, controlled_buffer_4_out,
       not_1_out, not_2_out, not_3_out, not_4_out, not_5_out, not_6_out, not_7_out, not_8_out, or_1_out,
       or_2_out, or_3_out, or_8_out;
  wire [11:0] and_9_out;
  wire [14:0] controlled_buffer_9_out;
  wire [25:0] ram_1_dout;

  not not_1 (not_1_out, irupt);
  not not_2 (not_2_out, EXM_EXEC_I);
  not not_3 (not_3_out, IS_EXM_I);
  or or_1 (or_1_out, irupt, DATA_SECTOR_I[0]);
  and and_1 (and_1_out, not_1_out, DATA_SECTOR_I[1]);
  and and_2 (and_2_out, not_1_out, DATA_SECTOR_I[2]);
  and and_3 (and_3_out, not_1_out, DATA_SECTOR_I[3]);
  and and_4 (and_4_out, OPADDR_I[0], not_3_out);
  and and_5 (and_5_out, OPADDR_I[1], not_3_out);
  and and_6 (and_6_out, OPADDR_I[2], not_3_out);
  and and_7 (and_7_out, OPADDR_I[3], not_3_out);
  and and_8 (and_8_out, OPADDR_I[4], not_3_out);
  or or_2 (or_2_out, OPADDR_I[7], IS_EXM_I);
  assign controlled_buffer_1_out = not_2_out ? or_1_out : 1'bz;  // Controlled_Buffer controlled_buffer_1
  assign controlled_buffer_2_out = not_2_out ? and_1_out : 1'bz;  // Controlled_Buffer controlled_buffer_2
  assign controlled_buffer_3_out = not_2_out ? and_2_out : 1'bz;  // Controlled_Buffer controlled_buffer_3
  assign controlled_buffer_4_out = not_2_out ? and_3_out : 1'bz;  // Controlled_Buffer controlled_buffer_4
  assign controlled_buffer_1_out = EXM_EXEC_I ? EXM_SECTOR[1] : 1'bz;  // Controlled_Buffer controlled_buffer_5
  assign controlled_buffer_2_out = EXM_EXEC_I ? EXM_SECTOR[2] : 1'bz;  // Controlled_Buffer controlled_buffer_6
  assign controlled_buffer_3_out = EXM_EXEC_I ? 1'b1 : 1'bz;  // Controlled_Buffer controlled_buffer_7
  assign controlled_buffer_4_out = EXM_EXEC_I ? EXM_SECTOR[0] : 1'bz;  // Controlled_Buffer controlled_buffer_8
  or or_3 (or_3_out, RESIDUAL_I, IS_EXM_I);
  and and_9 (and_9_out[0], and_4_out, not_1_out);
  and and_10 (and_9_out[1], and_5_out, not_1_out);
  and and_11 (and_9_out[2], and_6_out, not_1_out);
  and and_12 (and_9_out[3], and_7_out, not_1_out);
  and and_13 (and_9_out[4], and_8_out, not_1_out);
  and and_14 (and_9_out[5], OPADDR_I[5], not_1_out);
  and and_15 (and_9_out[6], OPADDR_I[6], not_1_out);
  and and_16 (and_9_out[7], or_2_out, not_1_out);
  and and_17 (and_17_out, not_2_out, or_3_out);
  or or_4 (and_9_out[8], controlled_buffer_1_out, and_17_out);
  or or_5 (and_9_out[9], and_17_out, controlled_buffer_2_out);
  or or_6 (and_9_out[10], controlled_buffer_3_out, and_17_out);
  or or_7 (and_9_out[11], and_17_out, controlled_buffer_4_out);
  and and_18 (and_18_out, and_9_out[8], and_9_out[9], and_9_out[10], and_9_out[11]);
  and and_19 (and_19_out, and_9_out[7], and_9_out[6], and_9_out[2], and_9_out[3]);
  and and_20 (and_20_out, and_9_out[4], and_9_out[5], 1'b1, 1'b1);
  and and_21 (and_21_out, and_18_out, and_19_out, and_20_out, 1'b1);
  not not_4 (not_4_out, and_9_out[1]);
  and and_22 (PQ_ADDR, and_9_out[0], not_4_out, not_6_out, and_21_out);
  and and_23 (HOP_INSTEAD_OF_A, and_9_out[1], and_21_out);
  not not_5 (not_5_out, PQ_ADDR);
  not not_6 (not_6_out, FETCH_CYC);
  and and_24 (and_24_out, FETCH_CYC, not_3_out);
  assign controlled_buffer_9_out = and_24_out ? {INSTR_MODULE_I, INSTR_SECTOR_I, PCI} : 15'bz;  // Controlled_Buffer controlled_buffer_9
  assign controlled_buffer_9_out = not_7_out ? {DATA_MODULE_I, and_9_out} : 15'bz;  // Controlled_Buffer controlled_buffer_10
  not not_7 (not_7_out, and_24_out);
  Hex_Digit_Display hex_digit_display_1 (.value({1'b0, controlled_buffer_9_out[14:12]}));  // open: dp
  Hex_Digit_Display hex_digit_display_2 (.value(controlled_buffer_9_out[11:8]));  // open: dp
  and and_25 (and_25_out, MEM_WR, not_5_out);
  RAM #(.addrWidth(15), .asyncread("true"), .dataWidth(26), .trigger("falling"), .\type ("nonvolatile")) ram_1 (
    .addr(controlled_buffer_9_out), .we(and_25_out), .oe(not_8_out), .clk(CLKIR), .din(M_BUSI),
    .dout(ram_1_dout));
  not not_8 (not_8_out, and_25_out);
  Hex_Digit_Display hex_digit_display_3 (.value(controlled_buffer_9_out[7:4]));  // open: dp
  Hex_Digit_Display hex_digit_display_4 (.value(controlled_buffer_9_out[3:0]));  // open: dp
  LED IS_FETCH (.in(and_24_out));
  assign M_BUSO = or_8_out ? ram_1_dout : 26'bz;  // Controlled_Buffer controlled_buffer_11
  and and_26 (and_26_out, MEM_RD, not_5_out);
  or or_8 (or_8_out, and_26_out, FETCH_CYC);
endmodule

module InstructionDecode (
  input  [10:0] DIN,
  output [15:0] DOUT
);

  ROM #(.addrWidth(11), .dataWidth(16)) rom_1 (.addr(DIN), .data(DOUT));

  // Notes on the sheet:
  //   contents of rom_1 (hex, n*v repeats v):
  //   400 880 20 5*0 400 0 c000 4010 8800 20 0 0 400 800 a 20 4*0 400 0 c000 4010 8800 20 0 0 400 100 20
  //   5*0 400 0 c000 4010 8800 0 c008 20 400 800 a 20 4*0 400 800 a 20 4*0 400 100 20 5*0 400 800 a 20 4*0
  //   400 20 6*0 400 210 10 20 4*0 400 0 20 5*0 400 800 a 20 4*0 400 40 20 5*0 400 800 a 20 4*0 400 880 20
  //   5*0 400 0 c000 4010 8800 20 0 0 400 800 a 20 4*0 400 0 c000 4010 8800 20 0 0 400 100 20 5*0 400 0
  //   c000 4010 8800 0 c008 20 400 800 a 20 4*0 400 800 a 20 4*0 400 100 20 5*0 400 800 a 20 4*0 400 20
  //   6*0 400 210 10 20 4*0 400 0 20 5*0 400 800 a 20 4*0 400 4 a 20 4*0 400 800 a 20 4*0 400 880 20 5*0
  //   400 0 c000 4010 8800 20 0 0 400 800 a 20 4*0 400 0 c000 4010 8800 20 0 0 400 100 20 5*0 400 0 c000
  //   4010 8800 0 c008 20 400 800 a 20 4*0 400 800 a 20 4*0 400 100 20 5*0 400 800 a 20 4*0 400 20 6*0 400
  //   210 10 20 4*0 400 0 20 5*0 400 800 a 20 4*0 400 40 20 5*0 400 800 a 20 4*0 400 880 20 5*0 400 0 c000
  //   4010 8800 20 0 0 400 800 a 20 4*0 400 0 c000 4010 8800 20 0 0 400 100 20 5*0 400 0 c000 4010 8800 0
  //   c008 20 400 800 a 20 4*0 400 800 a 20 4*0 400 100 20 5*0 400 800 a 20 4*0 400 20 6*0 400 210 10 20
  //   4*0 400 0 20 5*0 400 800 a 20 4*0 1400 1020 6*1000 400 800 a 20 4*0 400 880 20 5*0 400 0 c000 4010
  //   8800 20 0 0 400 800 a 20 4*0 400 0 c000 4010 8800 20 0 0 400 0 20 5*0 400 0 c000 4010 8800 0 c008 20
  //   400 800 a 20 4*0 400 800 a 20 4*0 400 100 20 5*0 400 800 a 20 4*0 400 20 6*0 400 210 10 20 4*0 400 0
  //   20 5*0 400 800 a 20 4*0 400 40 20 5*0 400 800 a 20 4*0 400 880 20 5*0 400 0 c000 4010 8800 20 0 0
  //   400 800 a 20 4*0 400 0 c000 4010 8800 20 0 0 400 0 20 5*0 400 0 c000 4010 8800 0 c008 20 400 800 a
  //   20 4*0 400 800 a 20 4*0 400 100 20 5*0 400 800 a 20 4*0 400 20 6*0 400 210 10 20 4*0 400 0 20 5*0
  //   400 800 a 20 4*0 400 4 a 20 4*0 400 800 a 20 4*0 400 880 20 5*0 400 0 c000 4010 8800 20 0 0 400 800
  //   a 20 4*0 400 0 c000 4010 8800 20 0 0 400 0 20 5*0 400 0 c000 4010 8800 0 c008 20 400 800 a 20 4*0
  //   400 800 a 20 4*0 400 100 20 5*0 400 800 a 20 4*0 400 20 6*0 400 210 10 20 4*0 400 0 20 5*0 400 800 a
  //   20 4*0 400 40 20 5*0 400 800 a 20 4*0 400 880 20 5*0 400 0 c000 4010 8800 20 0 0 400 800 a 20 4*0
  //   400 0 c000 4010 8800 20 0 0 400 0 20 5*0 400 0 c000 4010 8800 0 c008 20 400 800 a 20 4*0 400 800 a
  //   20 4*0 400 100 20 5*0 400 800 a 20 4*0 400 20 6*0 400 210 10 20 4*0 400 0 20 5*0 400 800 a 20 4*0
  //   1400 1020 6*1000 400 800 a 20 4*0 400 880 20 5*0 400 0 c000 4010 8800 20 0 0 400 800 a 20 4*0 400 0
  //   c000 4010 8800 20 0 0 400 100 20 5*0 400 0 c000 4010 8800 0 c008 20 400 800 a 20 4*0 400 800 a 20
  //   4*0 400 100 20 5*0 400 800 a 20 4*0 400 20 6*0 400 210 10 20 4*0 400 100 20 5*0 400 800 a 20 4*0 400
  //   40 20 5*0 400 800 a 20 4*0 400 880 20 5*0 400 0 c000 4010 8800 20 0 0 400 800 a 20 4*0 400 0 c000
  //   4010 8800 20 0 0 400 100 20 5*0 400 0 c000 4010 8800 0 c008 20 400 800 a 20 4*0 400 800 a 20 4*0 400
  //   100 20 5*0 400 800 a 20 4*0 400 20 6*0 400 210 10 20 4*0 400 100 20 5*0 400 800 a 20 4*0 400 4 a 20
  //   4*0 400 800 a 20 4*0 400 880 20 5*0 400 0 c000 4010 8800 20 0 0 400 800 a 20 4*0 400 0 c000 4010
  //   8800 20 0 0 400 100 20 5*0 400 0 c000 4010 8800 0 c008 20 400 800 a 20 4*0 400 800 a 20 4*0 400 100
  //   20 5*0 400 800 a 20 4*0 400 20 6*0 400 210 10 20 4*0 400 100 20 5*0 400 800 a 20 4*0 400 40 20 5*0
  //   400 800 a 20 4*0 400 880 20 5*0 400 0 c000 4010 8800 20 0 0 400 800 a 20 4*0 400 0 c000 4010 8800 20
  //   0 0 400 100 20 5*0 400 0 c000 4010 8800 0 c008 20 400 800 a 20 4*0 400 800 a 20 4*0 400 100 20 5*0
  //   400 800 a 20 4*0 400 20 6*0 400 210 10 20 4*0 400 100 20 5*0 400 800 a 20 4*0 1400 1020 6*1000 400
  //   800 a 20 117*0 40 20 13*0 400 880 20 5*0 400 0 c000 4010 8800 20 0 0 400 800 a 20 4*0 400 0 c000
  //   4010 8800 20 0 0 400 100 20 5*0 400 0 c000 4010 8800 0 c008 20 400 800 a 20 4*0 400 800 a 20 4*0 400
  //   100 20 5*0 400 800 a 20 4*0 400 20 6*0 400 210 10 20 4*0 400 100 20 5*0 400 800 a 20 4*0 400 4 a 20
  //   4*0 400 800 a 20 4*0 400 880 20 5*0 400 0 c000 4010 8800 20 0 0 400 800 a 20 4*0 400 0 c000 4010
  //   8800 20 0 0 400 100 20 5*0 400 0 c000 4010 8800 0 c008 20 400 800 a 20 4*0 400 800 a 20 4*0 400 100
  //   20 5*0 400 800 a 20 4*0 40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
endmodule

module muldiv (
  input  OUTPUT_PQ,
  input  RST,
  input  CLK,
  input  [25:0] MD_BUSI,
  input  LDX,
  input  LDY,
  input  IS_DIV,
  input  LDZ,
  input  START,
  output [25:0] MD_BUSO,
  output IS_ACTIVE
);

  wire and_1_out, and_2_out, and_3_out, and_4_out, and_5_out, and_6_out, and_7_out, and_8_out, and_9_out,
       and_10_out, and_11_out, and_12_out, and_13_out, and_14_out, and_15_out, and_16_out, and_17_out,
       and_18_out, and_19_out, and_20_out, DIVIDING_q, DIVIDING_qn, LAST_OP_q, ls74181_1_cnp4,
       ls74181_2_cnp4, ls74181_3_cnp4, ls74181_4_cnp4, ls74181_5_cnp4, ls74181_6_cnp4, ls74181_7_cnp4,
       ls74181_8_cnp4, ls74181_9_cnp4, ls74181_10_cnp4, ls74181_11_cnp4, ls74181_12_cnp4, MULTIPLYING_q,
       MULTIPLYING_qn, n74163_1_pin9, n74163_1_pin10, n74163_1_pin11, n74163_1_pin12, n74163_1_pin14,
       n74163_1_pin15, n74163_2_pin9, n74163_2_pin11, n74163_2_pin12, n74163_2_pin13, n74163_2_pin14,
       nand_1_out, nand_2_out, nand_3_out, nor_1_out, nor_2_out, not_1_out, not_2_out, not_3_out, not_4_out,
       not_5_out, not_6_out, not_7_out, or_1_out, or_2_out, or_3_out, or_4_out, or_5_out, or_8_out, or_9_out,
       or_10_out, or_11_out;
  wire [0:0] controlled_buffer_2_out_2, or_7_out;
  wire [22:0] controlled_buffer_2_out;
  wire [22:22] X_q_2;
  wire [23:1] X_q;
  wire [47:0] controlled_buffer_1_out, controlled_buffer_4_out, ls74181_1_f0b, Z_q;
  wire [47:1] Y_q;
  wire [47:47] Y_q_2;

  or or_1 (or_1_out, DIVIDING_q, MULTIPLYING_q);
  and and_1 (and_1_out, START, IS_DIV);
  and and_2 (and_2_out, DIVIDING_q, nand_3_out);
  and and_3 (and_3_out, not_3_out, START);
  and and_4 (and_4_out, MULTIPLYING_q, not_2_out);
  and and_5 (and_5_out, and_6_out, or_4_out);
  or or_2 (or_2_out, and_1_out, and_2_out);
  or or_3 (or_3_out, and_3_out, and_4_out);
  or or_4 (or_4_out, START, not_1_out);
  D_Flip_Flop MULTIPLYING (
    .D(or_3_out), .clk(CLK), .Q(MULTIPLYING_q), .Qn(MULTIPLYING_qn), .reset(RST));  // open: preset
  not not_1 (not_1_out, RST);
  _74163 u_74163_1 (
    .pin1(and_5_out), .pin2(CLK), .pin7(or_1_out), .pin15(n74163_1_pin15), .pin14(n74163_1_pin14),
    .pin12(n74163_1_pin12), .pin11(n74163_1_pin11), .pin10(n74163_1_pin10), .pin9(n74163_1_pin9));  // open: pin3, pin4, pin5, pin6, pin13
  _74163 u_74163_2 (
    .pin1(and_5_out), .pin2(CLK), .pin7(or_1_out), .pin14(n74163_2_pin14), .pin13(n74163_2_pin13),
    .pin12(n74163_2_pin12), .pin11(n74163_2_pin11), .pin10(n74163_1_pin15), .pin9(n74163_2_pin9));  // open: pin3, pin4, pin5, pin6, pin15
  D_Flip_Flop DIVIDING (.D(or_2_out), .clk(CLK), .Q(DIVIDING_q), .Qn(DIVIDING_qn), .reset(RST));  // open: preset
  D_Flip_Flop LAST_OP (.D(IS_DIV), .clk(START), .Q(LAST_OP_q));  // open: Qn, preset, reset
  nand nand_1 (nand_1_out, or_3_out, MULTIPLYING_qn);
  nand nand_2 (nand_2_out, or_2_out, DIVIDING_qn);
  and and_6 (and_6_out, nand_1_out, nand_2_out);
  and and_7 (and_7_out, n74163_1_pin11, MULTIPLYING_q, n74163_2_pin14);
  not not_2 (not_2_out, and_7_out);
  nand nand_3 (nand_3_out, n74163_2_pin14, n74163_2_pin13);
  not not_3 (not_3_out, IS_DIV);
  assign controlled_buffer_1_out = and_8_out ? {{24{1'b0}}, MD_BUSI[25:2]} : 48'bz;  // Controlled_Buffer controlled_buffer_1
  and and_8 (and_8_out, not_3_out, LDY);
  and and_9 (and_9_out, ~n74163_1_pin14, DIVIDING_q);  // AND_Gate
  and and_10 (and_10_out, n74163_1_pin14, DIVIDING_q);
  assign {controlled_buffer_2_out, controlled_buffer_2_out_2[0]} = LDX ? MD_BUSI[25:2] : 24'bz;  // Controlled_Buffer controlled_buffer_2
  and and_11 (and_11_out, LDY, IS_DIV);
  assign controlled_buffer_1_out = and_11_out ? {MD_BUSI[23:0], {24{1'b0}}} : 48'bz;  // Controlled_Buffer controlled_buffer_3
  assign controlled_buffer_4_out = LDZ ? {{24{1'b0}}, MD_BUSI[23:0]} : 48'bz;  // Controlled_Buffer controlled_buffer_4
  or or_5 (or_5_out, ~and_12_out, and_14_out);  // OR_Gate
  or or_6 (IS_ACTIVE, or_3_out, or_2_out);
  not not_4 (not_4_out, LDZ);
  assign controlled_buffer_4_out = not_4_out ? ls74181_1_f0b : 48'bz;  // Controlled_Buffer controlled_buffer_5
  and and_12 (and_12_out, DIVIDING_q, and_10_out);
  assign {controlled_buffer_2_out, controlled_buffer_2_out_2[0]} = and_10_out ? {X_q, 1'b0} : 24'bz;  // Controlled_Buffer LEFT
  assign {controlled_buffer_2_out, controlled_buffer_2_out_2[0]} = MULTIPLYING_q ? {1'b0, X_q_2[22], X_q[23:2]} : 24'bz;  // Controlled_Buffer RIGHT
  nor nor_1 (nor_1_out, and_10_out, LDX, MULTIPLYING_q);
  assign {controlled_buffer_2_out, controlled_buffer_2_out_2[0]} = nor_1_out ? {X_q_2[22], X_q} : 24'bz;  // Controlled_Buffer CENTER
  or or_7 (or_7_out[0], and_14_out, controlled_buffer_2_out_2[0]);
  Register #(.width(24)) X (
    .D({controlled_buffer_2_out, or_7_out[0]}), .en(1'b1), .clk(CLK), .Q({X_q_2[22], X_q}), .clr(RST));
  assign controlled_buffer_1_out = MULTIPLYING_q ? {Y_q, 1'b0} : 48'bz;  // Controlled_Buffer controlled_buffer_6
  nor nor_2 (nor_2_out, MULTIPLYING_q, LDY);
  assign controlled_buffer_1_out = nor_2_out ? {Y_q_2[47], Y_q} : 48'bz;  // Controlled_Buffer controlled_buffer_7
  Register #(.width(48)) Y (.D(controlled_buffer_1_out), .en(1'b1), .clk(CLK), .Q({Y_q_2[47], Y_q}), .clr(RST));
  Register #(.width(48)) Z (.D(controlled_buffer_4_out), .en(or_5_out), .clk(CLK), .Q(Z_q), .clr(RST));
  and and_13 (and_13_out, MULTIPLYING_q, X_q[1]);
  LED led_1 (.in(X_q[1]));
  and and_14 (and_14_out, DIVIDING_q, not_7_out);
  or or_8 (or_8_out, and_13_out, and_10_out, and_9_out);
  not not_5 (not_5_out, or_8_out);
  or or_9 (or_9_out, not_5_out, and_13_out, and_9_out);
  or or_10 (or_10_out, and_9_out, and_10_out);
  or or_11 (or_11_out, and_9_out, and_13_out);
  and and_15 (and_15_out, and_13_out, or_8_out);
  and and_16 (and_16_out, or_8_out, and_10_out);
  and and_17 (and_17_out, or_10_out, or_8_out);
  and and_18 (and_18_out, or_8_out, or_11_out);
  LS74181 ls74181_1 (
    .Cn(or_9_out), .M(1'b0), .A0b(Z_q[0]), .B0b(Y_q[1]), .A1b(Z_q[1]), .B1b(Y_q[2]), .A2b(Z_q[2]),
    .B2b(Y_q[3]), .A3b(Z_q[3]), .B3b(Y_q[4]), .S0(and_15_out), .S1(and_16_out), .S2(and_17_out),
    .S3(and_18_out), .F0b(ls74181_1_f0b[0]), .F1b(ls74181_1_f0b[1]), .F2b(ls74181_1_f0b[2]),
    .F3b(ls74181_1_f0b[3]), .Cnp4(ls74181_1_cnp4));  // open: AeqlB, Pb, Gp
  LS74181 ls74181_2 (
    .Cn(ls74181_1_cnp4), .M(1'b0), .A0b(Z_q[4]), .B0b(Y_q[5]), .A1b(Z_q[5]), .B1b(Y_q[6]), .A2b(Z_q[6]),
    .B2b(Y_q[7]), .A3b(Z_q[7]), .B3b(Y_q[8]), .S0(and_15_out), .S1(and_16_out), .S2(and_17_out),
    .S3(and_18_out), .F0b(ls74181_1_f0b[4]), .F1b(ls74181_1_f0b[5]), .F2b(ls74181_1_f0b[6]),
    .F3b(ls74181_1_f0b[7]), .Cnp4(ls74181_2_cnp4));  // open: AeqlB, Pb, Gp
  LS74181 ls74181_3 (
    .Cn(ls74181_2_cnp4), .M(1'b0), .A0b(Z_q[8]), .B0b(Y_q[9]), .A1b(Z_q[9]), .B1b(Y_q[10]), .A2b(Z_q[10]),
    .B2b(Y_q[11]), .A3b(Z_q[11]), .B3b(Y_q[12]), .S0(and_15_out), .S1(and_16_out), .S2(and_17_out),
    .S3(and_18_out), .F0b(ls74181_1_f0b[8]), .F1b(ls74181_1_f0b[9]), .F2b(ls74181_1_f0b[10]),
    .F3b(ls74181_1_f0b[11]), .Cnp4(ls74181_3_cnp4));  // open: AeqlB, Pb, Gp
  LS74181 ls74181_4 (
    .Cn(ls74181_3_cnp4), .M(1'b0), .A0b(Z_q[12]), .B0b(Y_q[13]), .A1b(Z_q[13]), .B1b(Y_q[14]), .A2b(Z_q[14]),
    .B2b(Y_q[15]), .A3b(Z_q[15]), .B3b(Y_q[16]), .S0(and_15_out), .S1(and_16_out), .S2(and_17_out),
    .S3(and_18_out), .F0b(ls74181_1_f0b[12]), .F1b(ls74181_1_f0b[13]), .F2b(ls74181_1_f0b[14]),
    .F3b(ls74181_1_f0b[15]), .Cnp4(ls74181_4_cnp4));  // open: AeqlB, Pb, Gp
  LS74181 ls74181_5 (
    .Cn(ls74181_4_cnp4), .M(1'b0), .A0b(Z_q[16]), .B0b(Y_q[17]), .A1b(Z_q[17]), .B1b(Y_q[18]), .A2b(Z_q[18]),
    .B2b(Y_q[19]), .A3b(Z_q[19]), .B3b(Y_q[20]), .S0(and_15_out), .S1(and_16_out), .S2(and_17_out),
    .S3(and_18_out), .F0b(ls74181_1_f0b[16]), .F1b(ls74181_1_f0b[17]), .F2b(ls74181_1_f0b[18]),
    .F3b(ls74181_1_f0b[19]), .Cnp4(ls74181_5_cnp4));  // open: AeqlB, Pb, Gp
  LS74181 ls74181_6 (
    .Cn(ls74181_5_cnp4), .M(1'b0), .A0b(Z_q[20]), .B0b(Y_q[21]), .A1b(Z_q[21]), .B1b(Y_q[22]), .A2b(Z_q[22]),
    .B2b(Y_q[23]), .A3b(Z_q[23]), .B3b(Y_q[24]), .S0(and_15_out), .S1(and_16_out), .S2(and_17_out),
    .S3(and_18_out), .F0b(ls74181_1_f0b[20]), .F1b(ls74181_1_f0b[21]), .F2b(ls74181_1_f0b[22]),
    .F3b(ls74181_1_f0b[23]), .Cnp4(ls74181_6_cnp4));  // open: AeqlB, Pb, Gp
  LS74181 ls74181_7 (
    .Cn(ls74181_6_cnp4), .M(1'b0), .A0b(Z_q[24]), .B0b(Y_q[25]), .A1b(Z_q[25]), .B1b(Y_q[26]), .A2b(Z_q[26]),
    .B2b(Y_q[27]), .A3b(Z_q[27]), .B3b(Y_q[28]), .S0(and_15_out), .S1(and_16_out), .S2(and_17_out),
    .S3(and_18_out), .F0b(ls74181_1_f0b[24]), .F1b(ls74181_1_f0b[25]), .F2b(ls74181_1_f0b[26]),
    .F3b(ls74181_1_f0b[27]), .Cnp4(ls74181_7_cnp4));  // open: AeqlB, Pb, Gp
  LS74181 ls74181_8 (
    .Cn(ls74181_7_cnp4), .M(1'b0), .A0b(Z_q[28]), .B0b(Y_q[29]), .A1b(Z_q[29]), .B1b(Y_q[30]), .A2b(Z_q[30]),
    .B2b(Y_q[31]), .A3b(Z_q[31]), .B3b(Y_q[32]), .S0(and_15_out), .S1(and_16_out), .S2(and_17_out),
    .S3(and_18_out), .F0b(ls74181_1_f0b[28]), .F1b(ls74181_1_f0b[29]), .F2b(ls74181_1_f0b[30]),
    .F3b(ls74181_1_f0b[31]), .Cnp4(ls74181_8_cnp4));  // open: AeqlB, Pb, Gp
  LS74181 ls74181_9 (
    .Cn(ls74181_8_cnp4), .M(1'b0), .A0b(Z_q[32]), .B0b(Y_q[33]), .A1b(Z_q[33]), .B1b(Y_q[34]), .A2b(Z_q[34]),
    .B2b(Y_q[35]), .A3b(Z_q[35]), .B3b(Y_q[36]), .S0(and_15_out), .S1(and_16_out), .S2(and_17_out),
    .S3(and_18_out), .F0b(ls74181_1_f0b[32]), .F1b(ls74181_1_f0b[33]), .F2b(ls74181_1_f0b[34]),
    .F3b(ls74181_1_f0b[35]), .Cnp4(ls74181_9_cnp4));  // open: AeqlB, Pb, Gp
  LS74181 ls74181_10 (
    .Cn(ls74181_9_cnp4), .M(1'b0), .A0b(Z_q[36]), .B0b(Y_q[37]), .A1b(Z_q[37]), .B1b(Y_q[38]), .A2b(Z_q[38]),
    .B2b(Y_q[39]), .A3b(Z_q[39]), .B3b(Y_q[40]), .S0(and_15_out), .S1(and_16_out), .S2(and_17_out),
    .S3(and_18_out), .F0b(ls74181_1_f0b[36]), .F1b(ls74181_1_f0b[37]), .F2b(ls74181_1_f0b[38]),
    .F3b(ls74181_1_f0b[39]), .Cnp4(ls74181_10_cnp4));  // open: AeqlB, Pb, Gp
  LS74181 ls74181_11 (
    .Cn(ls74181_10_cnp4), .M(1'b0), .A0b(Z_q[40]), .B0b(Y_q[41]), .A1b(Z_q[41]), .B1b(Y_q[42]),
    .A2b(Z_q[42]), .B2b(Y_q[43]), .A3b(Z_q[43]), .B3b(Y_q[44]), .S0(and_15_out), .S1(and_16_out),
    .S2(and_17_out), .S3(and_18_out), .F0b(ls74181_1_f0b[40]), .F1b(ls74181_1_f0b[41]),
    .F2b(ls74181_1_f0b[42]), .F3b(ls74181_1_f0b[43]), .Cnp4(ls74181_11_cnp4));  // open: AeqlB, Pb, Gp
  LS74181 ls74181_12 (
    .Cn(ls74181_11_cnp4), .M(1'b0), .A0b(Z_q[44]), .B0b(Y_q[45]), .A1b(Z_q[45]), .B1b(Y_q[46]),
    .A2b(Z_q[46]), .B2b(Y_q[47]), .A3b(Z_q[47]), .B3b(Y_q_2[47]), .S0(and_15_out), .S1(and_16_out),
    .S2(and_17_out), .S3(and_18_out), .F0b(ls74181_1_f0b[44]), .F1b(ls74181_1_f0b[45]),
    .F2b(ls74181_1_f0b[46]), .F3b(ls74181_1_f0b[47]), .Cnp4(ls74181_12_cnp4));  // open: AeqlB, Pb, Gp
  LED led_2 (.in(ls74181_1_f0b[47]));
  not not_6 (not_6_out, LAST_OP_q);
  D_Flip_Flop d_ff_1 (.D(ls74181_12_cnp4), .clk(CLK));  // open: Q, Qn, preset, reset
  and and_19 (and_19_out, OUTPUT_PQ, LAST_OP_q);
  and and_20 (and_20_out, OUTPUT_PQ, not_6_out);
  not not_7 (not_7_out, ls74181_12_cnp4);
  assign MD_BUSO = and_19_out ? {2'b00, X_q_2[22], X_q} : 26'bz;  // Controlled_Buffer controlled_buffer_8
  assign MD_BUSO = and_20_out ? Z_q[25:0] : 26'bz;  // Controlled_Buffer controlled_buffer_9
  // also tied to VCC on the sheet: {n74163_1_pin10, n74163_1_pin9, n74163_2_pin9}
endmodule
